# Fritzing sketch tips_motor_tb6612 (saved by Fritzing 0.9.3b)

parts:
  Part2 = Dagu Gear Motor
  Arduino2 = Arduino Uno (Rev3)
  BAT10 = Battery Holders [package=battery-aa-kit]
  BAT11 = Battery Holders [package=battery-aa-kit]
  BAT12 = Battery Holders [package=battery-aa-kit]
  BAT13 = Battery Holders [package=battery-aa-kit]
  PART2 = Motor Driver 1A Dual TB6612FNG [part_number=ROB_09457]

nets:
  N1: Part2.IN1, PART2.A01
  N2: Part2.IN2, PART2.A02
  N3: Arduino2.D8, PART2.AIN1
  N4: Arduino2.D13/SCK, PART2.STBY
  N5: Arduino2.D6_PWM, PART2.PWMA
  N6: Arduino2.D7, PART2.AIN2
  5V: Arduino2.5V, PART2.VCC
  N7: Arduino2.GND, PART2.GND#10
  N8: BAT10.+, PART2.VM
  N9: BAT10.-, BAT12.+
  N10: BAT11.+, BAT12.-
  N11: BAT11.-, BAT13.+
  N12: BAT13.-, PART2.GND#15

custom parts:
  Dagu Gear Motor: The most common hobbyist/kit dc motor on the market in 2016
  Motor Driver 1A Dual TB6612FNG: The TB6612FNG motor driver can control up to two DC motors at a constant current of 1.2A (3.2A peak). Two input signals (IN1 and IN2) can be used to control the motor in one of four function modes - CW, CCW, short-brake, and stop. The two motor outputs (A and B) can be separately controlled, the speed of each motor is controlled via a PWM input signal with a frequency up to 100kHz. The STBY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
